// Logisim project EvaluadorYRAM.circ as structural Verilog: 1 circuit, main circuit EvaluadorYRAM
module EvaluadorYRAM (
  input  [3:0] X,
  input  [3:0] Y,
  input  [15:0] F,
  input  Clock,
  input  Reset,
  input  Start,
  output [15:0] RAM_F,
  output RAM_LED
);

  wire comparator_1_eq, comparator_1_gt, MayorIgual;

  Comparator #(.width(16)) comparator_1 (
    .a(F), .b({16{1'b0}}), .gt(comparator_1_gt), .eq(comparator_1_eq));  // open: lt
  or or_1 (MayorIgual, comparator_1_gt, comparator_1_eq);
  RAM #(.clearpin("true"), .dataWidth(16)) F_RAM (
    .addr({Y, X}), .we(Start), .oe(Start), .clk(Clock), .din(F), .dout(RAM_F), .clr(Reset));
  RAM #(.clearpin("true"), .dataWidth(1)) LED_RAM (
    .addr({Y, X}), .we(Start), .oe(Start), .clk(Clock), .din(MayorIgual), .dout(RAM_LED), .clr(Reset));

  // Other names for the same wires on the sheet: Address[7:0] = {Y, X}

  // Notes on the sheet:
  //   RAM_F
  //   RAM_LED
endmodule
