// Logisim project GeneradorPixeles.circ as structural Verilog: 1 circuit, main circuit GeneradorPixeles
module GeneradorPixeles (
  input  in_1,
  input  in_2,
  input  in_3,
  input  in_4,
  input  Start,
  input  Reset,
  input  Clock,
  output [3:0] X,
  output [3:0] Y
);

  wire contadorx_1_carry;

  contadorX contadorx_1 (
    .Reset(Reset), .in_2(in_1), .in_3(in_3), .Start(Start), .Clock(Clock), .Carry(contadorx_1_carry), .X(X));
  contadorY contadory_1 (
    .Reset(Reset), .in_2(in_2), .in_3(in_4), .Start(contadorx_1_carry), .Clock(Clock), .Y(Y));  // open: Carry

  // Notes on the sheet:
  //   in_3: initial=0x1
  //   in_4: initial=0x1
endmodule
