// Logisim project contadorX.circ as structural Verilog: 1 circuit, main circuit contadorX
module contadorX (
  input  Reset,
  input  Enable,
  input  Clock,
  output Carry,
  output [3:0] X
);

  Counter #(.max('hf), .width(4)) counter_1 (
    .clr(Reset), .load(1'b0), .up(1'b1), .count(Enable), .clk(Clock), .D(4'b0000), .carry(Carry), .Q(X));
endmodule
