// Logisim project contadorY.circ as structural Verilog: 1 circuit, main circuit contadorY
module contadorY (
  input  Reset,
  input  Enable,
  input  Clock,
  output Carry,
  output [3:0] Y
);

  Counter #(.max('hf), .width(4)) counter_1 (
    .clr(Reset), .load(1'b0), .up(1'b1), .count(Enable), .clk(Clock), .D(4'b0000), .carry(Carry), .Q(Y));
endmodule
